// Logisim project sapcpu3.circ as structural Verilog: 2 circuits, main circuit main
// Reg
module main (
  input  [7:0] I__Input,
  input  [15:0] in_2,
  output [7:0] out_3,
  output [7:0] E__ALU,
  output [7:0] O__Output,
  output [7:0] MAR,
  output [7:0] out_7,
  output [7:0] out_8
);

  wire CLK_out;
  wire [7:0] ram_1_data;
  wire [15:0] rom_1_data;

  Clock CLK (.out(CLK_out));
  Register A (.D(out_8), .CLK(CLK_out), .RI(rom_1_data[15]), .RO(rom_1_data[14]), .Q(out_8), .V(out_3));
  Register B (.D(out_8), .CLK(CLK_out), .RI(rom_1_data[13]), .RO(rom_1_data[12]), .Q(out_8), .V(out_7));
  assign out_8 = rom_1_data[11] ? E__ALU : 8'bz;  // Controlled_Buffer controlled_buffer_1
  Adder adder_1 (.a(out_3), .b(out_7), .out(E__ALU));  // open: cin, cout
  assign out_8 = rom_1_data[10] ? I__Input : 8'bz;  // Controlled_Buffer controlled_buffer_2
  Register register_1 (.D(out_8), .CLK(CLK_out), .RI(rom_1_data[9]), .V(O__Output));  // open: RO, Q
  Register M_AR (.D(out_8), .CLK(CLK_out), .RI(rom_1_data[8]), .V(MAR));  // open: RO, Q
  RAM ram_1 (.addr(MAR), .data(ram_1_data), .clk(CLK_out));  // open: sel, ld, clr
  assign out_8 = rom_1_data[7] ? ram_1_data : 8'bz;  // Controlled_Buffer controlled_buffer_3
  ROM #(.addrWidth(16), .dataWidth(16)) rom_1 (.addr(in_2), .data(rom_1_data));  // open: sel

  // Notes on the sheet:
  //   SAP-1 inspireret 8 bit computer - version 2
  //   Michell Cronberg
  //   AO
  //   AI
  //   BI
  //   IO
  //   EO
  //   BO
  //   8 bit databus
  //   OI
  //   MI
  //   RO
  //   (R)AM
  //   contents of rom_1 (hex, n*v repeats v):
  //   500 8080
endmodule

module Register (
  input  RO,
  input  [7:0] D,
  input  CLK,
  input  RI,
  output [7:0] Q,
  output [7:0] V
);

  wire [7:0] controlled_buffer_1_out;

  assign controlled_buffer_1_out = RI ? D : 8'bz;  // Controlled_Buffer controlled_buffer_1
  Register_part register_1 (.D(controlled_buffer_1_out), .en(1'b1), .Q(V), .clk(CLK), .clr(1'b0));
  assign Q = RO ? V : 8'bz;  // Controlled_Buffer controlled_buffer_2
endmodule
