// Logisim project sapcpu4.circ as structural Verilog: 5 circuits, main circuit main
// Reg
module main (
  input  [7:0] K__Input,
  input  [15:0] in_2,
  output [7:0] out_3,
  output [7:0] out_4,
  output [7:0] E__ALU,
  output [7:0] O__Output,
  output [7:0] MAR,
  output [7:0] out_8,
  output [7:0] out_9,
  output [7:0] out_10
);

  wire CLK_out;
  wire [7:0] controlled_buffer_3_out, ram_1_data;
  wire [15:0] rom_1_data;

  Clock CLK (.out(CLK_out));
  Register IR (.D(out_9), .CLK(CLK_out), .RI(rom_1_data[3]), .RO(rom_1_data[2]), .Q(out_9), .V(out_10));
  Register A (.D(out_9), .CLK(CLK_out), .RI(rom_1_data[15]), .RO(rom_1_data[14]), .Q(out_9), .V(out_4));
  Register B (.D(out_9), .CLK(CLK_out), .RI(rom_1_data[13]), .RO(rom_1_data[12]), .Q(out_9), .V(out_8));
  assign out_9 = rom_1_data[11] ? E__ALU : 8'bz;  // Controlled_Buffer controlled_buffer_1
  Adder adder_1 (.a(out_4), .b(out_8), .out(E__ALU));  // open: cin, cout
  assign out_9 = rom_1_data[10] ? K__Input : 8'bz;  // Controlled_Buffer controlled_buffer_2
  Register register_1 (.D(out_9), .CLK(CLK_out), .RI(rom_1_data[9]), .V(O__Output));  // open: RO, Q
  Register M_AR (.D(out_9), .CLK(CLK_out), .RI(rom_1_data[8]), .V(MAR));  // open: RO, Q
  ROM #(.addrWidth(16), .dataWidth(16)) rom_1 (.addr(in_2), .data(rom_1_data));  // open: sel
  assign controlled_buffer_3_out = rom_1_data[5] ? out_9 : 8'bz;  // Controlled_Buffer controlled_buffer_3
  RAM ram_1 (.addr(MAR), .data(ram_1_data), .clk(CLK_out));  // open: sel, ld, clr
  assign out_9 = rom_1_data[7] ? ram_1_data : 8'bz;  // Controlled_Buffer controlled_buffer_4
  ProgramCounter PC (.S(rom_1_data[5]), .A(controlled_buffer_3_out), .Count(rom_1_data[6]), .Q(out_3));  // open: Reset
  assign out_9 = rom_1_data[4] ? out_3 : 8'bz;  // Controlled_Buffer controlled_buffer_5

  // Notes on the sheet:
  //   SAP-1 inspireret 8 bit computer - version 4
  //   Michell Cronberg
  //   BI
  //   AO
  //   AI
  //   BO
  //   EO
  //   KO
  //   8 bit databus
  //   MI
  //   OI
  //   II
  //   IO
  //   RO
  //   PE
  //   PI
  //   PO
  //   0110
  //   (R)AM
  //   contents of rom_1 (hex, n*v repeats v):
  //   110 88 40 340 8080 0 110 88
endmodule

module Register (
  input  RO,
  input  [7:0] D,
  input  CLK,
  input  RI,
  output [7:0] Q,
  output [7:0] V
);

  wire [7:0] controlled_buffer_1_out;

  assign controlled_buffer_1_out = RI ? D : 8'bz;  // Controlled_Buffer controlled_buffer_1
  Register_part register_1 (.D(controlled_buffer_1_out), .en(1'b1), .Q(V), .clk(CLK), .clr(1'b0));
  assign Q = RO ? V : 8'bz;  // Controlled_Buffer controlled_buffer_2
endmodule

module ProgramCounter (
  input  S,
  input  [7:0] A,
  input  Count,
  input  Reset,
  output [7:0] Q
);

  wire not_1_out;

  not not_1 (not_1_out, S);
  Counter counter_1 (.load(S), .D(A), .count(not_1_out), .Q(Q), .clk(Count), .clr(Reset));  // open: carry
endmodule

module SplitByteLower4 (
  input  [7:0] A,
  output [7:0] Q
);


  assign Q = {4'b0000, A[3:0]};
endmodule

module MircoInstructionAddress (
  input  [3:0] in_1,
  output [15:0] out_2
);


  assign out_2 = {{8{1'b0}}, in_1, 4'b0000};
endmodule
